# Fritzing sketch button Sketch (saved by Fritzing 0.9.3b)
breadboards: 1

parts:
  LED1 = LED - 5mm [color="Red (633nm)" package="5 mm [THT]"]
  S1 = Pushbutton [package="[THT]"]
  Part1 = Arduino Uno (Rev3)

nets:
  N1: LED1.cathode, S1.Pin_1, S1.Pin_2
  N2: LED1.anode, Part1.D5_PWM
  N3: S1.Pin_3, S1.Pin_4, Part1.D7

// code stored in the sketch: button.ino

// Gourida Said(Said113)





int btn = 7; 


int led = 5; 


int btnState = 0; // this will take the value of the btn(pin7)





void setup() {


pinMode(ledPin, OUTPUT); 


pinMode(buttonPin, INPUT); 


}





void loop(){


btnState = digitalRead(btn); // is this situation we need to use the digitalread function to read the btn is on mean (1) or off is (0) 


// when you press the button the btnState will be 1 and vice versa


if (btnState == 1) { 


digitalWrite(led, HIGH); //this will turn LED on: 


} 


else{


digitalWrite(led, LOW); //this will turn LED off:


}

}
