# Fritzing sketch rgbled (saved by Fritzing 0.9.3b)
breadboards: 1

parts:
  Part1 = Arduino Uno (Rev3)
  LED3 = RGB LED (com. cathode, rgb) [package="5 mm [THT]"]

nets:
  N1: Part1.D1/TX, LED3.red_anode
  N2: Part1.D2, LED3.green_anode
  N3: Part1.D3_PWM, LED3.blue_anode

// code stored in the sketch: button.ino

// Gourida Said(Said113)





int btn = 7; 


int led = 5; 


int btnState = 0; // this will take the value of the btn(pin7)





void setup() {


pinMode(ledPin, OUTPUT); 


pinMode(buttonPin, INPUT); 


}





void loop(){


btnState = digitalRead(btn); // is this situation we need to use the digitalread function to read the btn is on mean (1) or off is (0) 


// when you press the button the btnState will be 1 and vice versa


if (btnState == 1) { 


digitalWrite(led, HIGH); //this will turn LED on: 


} 


else{


digitalWrite(led, LOW); //this will turn LED off:


}

}
